# Fritzing sketch QuickTempController (saved by Fritzing 1.0.4)
breadboards: 1

parts:
  WeMos_D1_Mini1 = WeMos D1 Mini
  J1 = screw terminal, 3 pins
  DS1 = DS18B20 1-Wire Temperature Sensor Probe
  J2 = screw terminal, 2 pins
  R1 = Resistor [tolerance=±5% resistance=4.7k package="0603 [SMD]"]

nets:
  3V3: WeMos_D1_Mini1.3V3, J1.pin1, DS1.VDD, R1.Pin_0
  N1: WeMos_D1_Mini1.D3, J1.pin2, DS1.DQ, R1.Pin_1
  N2: WeMos_D1_Mini1.D5, J2.pin1
  N3: WeMos_D1_Mini1.G, J1.pin3, DS1.GND, J2.pin2

notes:
  To IoT Relay + and -

custom parts:
  WeMos D1 Mini: The D1 mini is a mini wifi board based on ESP-8266EX.
